// Logisim project Mid Answer.circ as structural Verilog: 5 circuits, main circuit main
module main (
);


  // Notes on the sheet:
  //   Md. Rifat Ahmed
  //   ID: 1931725042
  //   Mid Term
endmodule

// 3bit X 3bit
module _3_bit_X_3_bit_Multplier (
  input  [2:0] C,
  input  [2:0] D,
  output [5:0] out_3
);

  wire [1:0] and_8_out;
  wire [2:0] adder_1_out, and_3_out, and_6_out;

  and and_1 (and_3_out[2], D[2], C[2]);
  and and_2 (and_3_out[1], D[2], C[1]);
  and and_3 (and_3_out[0], D[2], C[0]);
  and and_4 (and_6_out[2], D[1], C[2]);
  and and_5 (and_6_out[1], D[1], C[1]);
  and and_6 (and_6_out[0], D[1], C[0]);
  and and_7 (and_8_out[1], D[0], C[2]);
  and and_8 (and_8_out[0], D[0], C[1]);
  and and_9 (out_3[0], D[0], C[0]);
  Adder #(.width(3)) adder_1 (
    .a({1'b0, and_8_out}), .b(and_6_out), .out({adder_1_out[1:0], out_3[1]}), .cin(1'b0),
    .cout(adder_1_out[2]));
  Adder #(.width(3)) adder_2 (.a(adder_1_out), .b(and_3_out), .out(out_3[4:2]), .cin(1'b0), .cout(out_3[5]));

  // Notes on the sheet:
  //   Question 1
endmodule

// 1-bit ALU
module _1_bit_ALU__AND__OR (
  input  C,
  input  D,
  input  [1:0] S1S0,
  output Result
);

  wire and_1_out, or_1_out;

  and and_1 (and_1_out, C, D);
  or or_1 (or_1_out, C, D);
  Multiplexer #(.select(2), .enable("false")) multiplexer_1 (
    .in0(and_1_out), .in1(or_1_out), .out(Result), .sel(S1S0));  // open: in2, in3

  // Notes on the sheet:
  //   1-bit ALU for AND and OR
endmodule

module _6_bit_ALU__AND__OR (
  input  [5:0] C,
  input  [5:0] D,
  input  [1:0] S1S0,
  output [5:0] Result
);

  _1_bit_ALU__AND__OR u_1_bit_alu_and_or_1 (.C(C[0]), .D(D[0]), .S1S0(S1S0), .Result(Result[0]));
  _1_bit_ALU__AND__OR u_1_bit_alu_and_or_2 (.C(C[1]), .D(D[1]), .S1S0(S1S0), .Result(Result[1]));
  _1_bit_ALU__AND__OR u_1_bit_alu_and_or_3 (.C(C[2]), .D(D[2]), .S1S0(S1S0), .Result(Result[2]));
  _1_bit_ALU__AND__OR u_1_bit_alu_and_or_4 (.C(C[3]), .D(D[3]), .S1S0(S1S0), .Result(Result[3]));
  _1_bit_ALU__AND__OR u_1_bit_alu_and_or_5 (.C(C[4]), .D(D[4]), .S1S0(S1S0), .Result(Result[4]));
  _1_bit_ALU__AND__OR u_1_bit_alu_and_or_6 (.C(C[5]), .D(D[5]), .S1S0(S1S0), .Result(Result[5]));

  // Notes on the sheet:
  //   6-bit ALU for AND and OR
endmodule

module _6_bit_ALU (
  input  [5:0] C,
  input  [5:0] D,
  input  [1:0] S1S0,
  output [5:0] Result
);

  wire [5:0] n3_bit_x_3_bit_multplier_1_out_3, n6_bit_alu_and_or_1_result;

  _6_bit_ALU__AND__OR u_6_bit_alu_and_or_1 (.C(C), .D(D), .S1S0(S1S0), .Result(n6_bit_alu_and_or_1_result));
  _3_bit_X_3_bit_Multplier u_3_bit_x_3_bit_multplier_1 (
    .C(C[2:0]), .D(D[2:0]), .out_3(n3_bit_x_3_bit_multplier_1_out_3));
  Multiplexer #(.select(2), .width(6), .enable("false")) multiplexer_1 (
    .in0(n6_bit_alu_and_or_1_result), .in1(n6_bit_alu_and_or_1_result),
    .in3(n3_bit_x_3_bit_multplier_1_out_3), .out(Result), .sel(S1S0));  // open: in2

  // Notes on the sheet:
  //   Select Bits | Operation
  //   6-bit ALU for AND, OR and Multiplication
  //   00     |     AND
  //   01     |     OR
  //   11     |     Multiplication
endmodule
