// Logisim project CSE332.9-1931725042-Md. Rifat Ahmed-LAB HW 1-Design of a 32-bit Logic unit.circ as structural Verilog
// 1-bit LU
module _1_bit_Logic_Unit (
  input  A,
  input  B,
  input  [1:0] S1S0,
  output F
);

  wire and_1_out, not_1_out, or_1_out, xor_1_out;

  and and_1 (and_1_out, A, B);
  or or_1 (or_1_out, A, B);
  xor xor_1 (xor_1_out, A, B);
  not not_1 (not_1_out, A);
  Multiplexer #(.select(2)) multiplexer_1 (
    .in0(and_1_out), .in1(or_1_out), .in2(xor_1_out), .in3(not_1_out), .out(F), .sel(S1S0));  // open: en

  // Notes on the sheet:
  //   1-bit Logic Unit
endmodule

// 2-bit LU
module _2_bit_Logic_Unit (
  input  [1:0] A,
  input  [1:0] B,
  input  [1:0] S1S0,
  output [1:0] F
);

  _1_bit_Logic_Unit _0 (.A(A[0]), .B(B[0]), .S1S0(S1S0), .F(F[0]));
  _1_bit_Logic_Unit _1 (.A(A[1]), .B(B[1]), .S1S0(S1S0), .F(F[1]));

  // Notes on the sheet:
  //   A0
  //   A1
  //   B0
  //   B1
  //   2-bit Logic Unit
endmodule

// 8-bit LU
module _8_bit_Logic_Unit (
  input  [7:0] A,
  input  [7:0] B,
  input  [1:0] S1S0,
  output [7:0] F
);

  _2_bit_Logic_Unit _0 (.A(A[1:0]), .B(B[1:0]), .S1S0(S1S0), .F(F[1:0]));
  _2_bit_Logic_Unit _1 (.A(A[3:2]), .B(B[3:2]), .S1S0(S1S0), .F(F[3:2]));
  _2_bit_Logic_Unit _2 (.A(A[5:4]), .B(B[5:4]), .S1S0(S1S0), .F(F[5:4]));
  _2_bit_Logic_Unit _3 (.A(A[7:6]), .B(B[7:6]), .S1S0(S1S0), .F(F[7:6]));

  // Notes on the sheet:
  //   8-bit Logic Unit
endmodule

// 32-bit LU
module _32_bit_Logic_Unit (
  input  [31:0] A,
  input  [31:0] B,
  input  [1:0] S1S0,
  output [31:0] F
);

  _8_bit_Logic_Unit u_8_bit_logic_unit_1 (.A(A[7:0]), .B(B[7:0]), .S1S0(S1S0), .F(F[7:0]));
  _8_bit_Logic_Unit u_8_bit_logic_unit_2 (.A(A[15:8]), .B(B[15:8]), .S1S0(S1S0), .F(F[15:8]));
  _8_bit_Logic_Unit u_8_bit_logic_unit_3 (.A(A[23:16]), .B(B[23:16]), .S1S0(S1S0), .F(F[23:16]));
  _8_bit_Logic_Unit u_8_bit_logic_unit_4 (.A(A[31:24]), .B(B[31:24]), .S1S0(S1S0), .F(F[31:24]));

  // Notes on the sheet:
  //   32-bit Logic Unit
  //   Md. Rifat Ahmed
  //   ID: 1931725042
endmodule
