// Logisim project CSE332.9-1931725042-Md. Rifat Ahmed-LAB HW 2-Design of a 32-bit Arithmetic unit.circ as structural Verilog
// 1-bit LU
module _1_bit_Logic_Unit (
  input  A,
  input  B,
  input  [1:0] S1S0,
  output F
);

  wire and_1_out, not_1_out, or_1_out, xor_1_out;

  and and_1 (and_1_out, A, B);
  or or_1 (or_1_out, A, B);
  xor xor_1 (xor_1_out, A, B);
  not not_1 (not_1_out, A);
  Multiplexer #(.select(2)) multiplexer_1 (
    .in0(and_1_out), .in1(or_1_out), .in2(xor_1_out), .in3(not_1_out), .out(F), .sel(S1S0));  // open: en

  // Notes on the sheet:
  //   1-bit Logic Unit
endmodule

// 2-bit LU
module _2_bit_Logic_Unit (
  input  [1:0] A,
  input  [1:0] B,
  input  [1:0] S1S0,
  output [1:0] F
);

  _1_bit_Logic_Unit _0 (.A(A[0]), .B(B[0]), .S1S0(S1S0), .F(F[0]));
  _1_bit_Logic_Unit _1 (.A(A[1]), .B(B[1]), .S1S0(S1S0), .F(F[1]));

  // Notes on the sheet:
  //   A0
  //   A1
  //   B0
  //   B1
  //   2-bit Logic Unit
endmodule

// 8-bit LU
module _8_bit_Logic_Unit (
  input  [7:0] A,
  input  [7:0] B,
  input  [1:0] S1S0,
  output [7:0] F
);

  _2_bit_Logic_Unit _0_1 (.A(A[1:0]), .B(B[1:0]), .S1S0(S1S0), .F(F[1:0]));
  _2_bit_Logic_Unit _2_3 (.A(A[3:2]), .B(B[3:2]), .S1S0(S1S0), .F(F[3:2]));
  _2_bit_Logic_Unit _4_5 (.A(A[5:4]), .B(B[5:4]), .S1S0(S1S0), .F(F[5:4]));
  _2_bit_Logic_Unit _6_7 (.A(A[7:6]), .B(B[7:6]), .S1S0(S1S0), .F(F[7:6]));

  // Notes on the sheet:
  //   8-bit Logic Unit
endmodule

// 32-bit LU
module _32_bit_Logic_Unit (
  input  [31:0] A,
  input  [31:0] B,
  input  [1:0] S1S0,
  output [31:0] F
);

  _8_bit_Logic_Unit u_8_bit_logic_unit_1 (.A(A[7:0]), .B(B[7:0]), .S1S0(S1S0), .F(F[7:0]));
  _8_bit_Logic_Unit u_8_bit_logic_unit_2 (.A(A[15:8]), .B(B[15:8]), .S1S0(S1S0), .F(F[15:8]));
  _8_bit_Logic_Unit u_8_bit_logic_unit_3 (.A(A[23:16]), .B(B[23:16]), .S1S0(S1S0), .F(F[23:16]));
  _8_bit_Logic_Unit u_8_bit_logic_unit_4 (.A(A[31:24]), .B(B[31:24]), .S1S0(S1S0), .F(F[31:24]));

  // Notes on the sheet:
  //   32-bit Logic Unit
  //   Md. Rifat Ahmed
  //   ID: 1931725042
endmodule

// 1-bit AU
module _1_bit_Arithmetic_Unit (
  input  Cin,
  input  A,
  input  B,
  input  [1:0] S1S0,
  output D,
  output Cout
);

  wire multiplexer_1_out, not_1_out;

  not not_1 (not_1_out, B);
  Multiplexer #(.select(2), .enable("false")) multiplexer_1 (
    .in0(B), .in1(not_1_out), .in2(1'b0), .in3(1'b1), .out(multiplexer_1_out), .sel(S1S0));
  Adder #(.width(1)) adder_1 (.a(A), .b(multiplexer_1_out), .out(D), .cin(Cin), .cout(Cout));

  // Notes on the sheet:
  //   1-bit Arithmetic Unit
endmodule

// 2-bit AU
module _2_bit_Arithmetic_Unit (
  input  Cin,
  input  [1:0] A1A0,
  input  [1:0] B1B0,
  input  [1:0] S1S0,
  output [1:0] D1D0,
  output Cout
);

  wire _0_cout;

  _1_bit_Arithmetic_Unit _0 (.Cin(Cin), .A(A1A0[0]), .B(B1B0[0]), .S1S0(S1S0), .D(D1D0[0]), .Cout(_0_cout));
  _1_bit_Arithmetic_Unit _1 (.Cin(_0_cout), .A(A1A0[1]), .B(B1B0[1]), .S1S0(S1S0), .D(D1D0[1]), .Cout(Cout));

  // Notes on the sheet:
  //   2-bit Arithmetic Unit
endmodule

// 8-bit AU
module _8_bit_Arithmetic_Unit (
  input  Cin,
  input  [7:0] A7_A0,
  input  [7:0] B7_B0,
  input  [1:0] S1S0,
  output [7:0] D7_D0,
  output Cout
);

  wire _0_1_cout, _2_3_cout, _4_5_cout;

  _2_bit_Arithmetic_Unit _0_1 (
    .Cin(Cin), .A1A0(A7_A0[1:0]), .B1B0(B7_B0[1:0]), .S1S0(S1S0), .D1D0(D7_D0[1:0]), .Cout(_0_1_cout));
  _2_bit_Arithmetic_Unit _2_3 (
    .Cin(_0_1_cout), .A1A0(A7_A0[3:2]), .B1B0(B7_B0[3:2]), .S1S0(S1S0), .D1D0(D7_D0[3:2]), .Cout(_2_3_cout));
  _2_bit_Arithmetic_Unit _4_5 (
    .Cin(_2_3_cout), .A1A0(A7_A0[5:4]), .B1B0(B7_B0[5:4]), .S1S0(S1S0), .D1D0(D7_D0[5:4]), .Cout(_4_5_cout));
  _2_bit_Arithmetic_Unit _6_7 (
    .Cin(_4_5_cout), .A1A0(A7_A0[7:6]), .B1B0(B7_B0[7:6]), .S1S0(S1S0), .D1D0(D7_D0[7:6]), .Cout(Cout));

  // Notes on the sheet:
  //   8-bit Arithmetic Unit
endmodule

module _32_bit_Arithmetic_Unit (
  input  Cin,
  input  [31:0] A31_A0,
  input  [31:0] B31_B0,
  input  [1:0] S1S0,
  output [31:0] D31_D0,
  output Cout
);

  wire _0_7_cout, _8_15_cout, _16_23_cout;

  _8_bit_Arithmetic_Unit _0_7 (
    .Cin(Cin), .A7_A0(A31_A0[7:0]), .B7_B0(B31_B0[7:0]), .S1S0(S1S0), .D7_D0(D31_D0[7:0]), .Cout(_0_7_cout));
  _8_bit_Arithmetic_Unit _8_15 (
    .Cin(_0_7_cout), .A7_A0(A31_A0[15:8]), .B7_B0(B31_B0[15:8]), .S1S0(S1S0), .D7_D0(D31_D0[15:8]),
    .Cout(_8_15_cout));
  _8_bit_Arithmetic_Unit _16_23 (
    .Cin(_8_15_cout), .A7_A0(A31_A0[23:16]), .B7_B0(B31_B0[23:16]), .S1S0(S1S0), .D7_D0(D31_D0[23:16]),
    .Cout(_16_23_cout));
  _8_bit_Arithmetic_Unit _24_31 (
    .Cin(_16_23_cout), .A7_A0(A31_A0[31:24]), .B7_B0(B31_B0[31:24]), .S1S0(S1S0), .D7_D0(D31_D0[31:24]),
    .Cout(Cout));

  // Notes on the sheet:
  //   32-bit Arithmetic Unit
  //   Md. Rifat Ahmed
  //   ID: 1931725042
endmodule
