// Logisim project CSE332.9-1931725042-Md. Rifat Ahmed-LAB HW 3-Design of a 16-bit by 16-bit Binary Multiplication Unit.circ as structural Verilog
module _1_bit_LU (
  input  A,
  input  B,
  input  [1:0] S1S0,
  output F
);

  wire and_1_out, not_1_out, or_1_out, xor_1_out;

  and and_1 (and_1_out, A, B);
  or or_1 (or_1_out, A, B);
  xor xor_1 (xor_1_out, A, B);
  not not_1 (not_1_out, A);
  Multiplexer #(.select(2)) multiplexer_1 (
    .in0(and_1_out), .in1(or_1_out), .in2(xor_1_out), .in3(not_1_out), .out(F), .sel(S1S0));  // open: en

  // Notes on the sheet:
  //   1-bit Logic Unit
endmodule

module _2_bit_LU (
  input  [1:0] A,
  input  [1:0] B,
  input  [1:0] S1S0,
  output [1:0] F
);

  _1_bit_LU _0 (.A(A[0]), .B(B[0]), .S1S0(S1S0), .F(F[0]));
  _1_bit_LU _1 (.A(A[1]), .B(B[1]), .S1S0(S1S0), .F(F[1]));

  // Notes on the sheet:
  //   A0
  //   A1
  //   B0
  //   B1
  //   2-bit Logic Unit
endmodule

module _8_bit_LU (
  input  [7:0] A,
  input  [7:0] B,
  input  [1:0] S1S0,
  output [7:0] F
);

  _2_bit_LU _0_1 (.A(A[1:0]), .B(B[1:0]), .S1S0(S1S0), .F(F[1:0]));
  _2_bit_LU _2_3 (.A(A[3:2]), .B(B[3:2]), .S1S0(S1S0), .F(F[3:2]));
  _2_bit_LU _4_5 (.A(A[5:4]), .B(B[5:4]), .S1S0(S1S0), .F(F[5:4]));
  _2_bit_LU _6_7 (.A(A[7:6]), .B(B[7:6]), .S1S0(S1S0), .F(F[7:6]));

  // Notes on the sheet:
  //   8-bit Logic Unit
endmodule

// 32-bit LU
module _32_bit_Logic_Unit (
  input  [31:0] A,
  input  [31:0] B,
  input  [1:0] S1S0,
  output [31:0] F
);

  _8_bit_LU u_8_bit_lu_1 (.A(A[7:0]), .B(B[7:0]), .S1S0(S1S0), .F(F[7:0]));
  _8_bit_LU u_8_bit_lu_2 (.A(A[15:8]), .B(B[15:8]), .S1S0(S1S0), .F(F[15:8]));
  _8_bit_LU u_8_bit_lu_3 (.A(A[23:16]), .B(B[23:16]), .S1S0(S1S0), .F(F[23:16]));
  _8_bit_LU u_8_bit_lu_4 (.A(A[31:24]), .B(B[31:24]), .S1S0(S1S0), .F(F[31:24]));

  // Notes on the sheet:
  //   32-bit Logic Unit
  //   Md. Rifat Ahmed
  //   ID: 1931725042
endmodule

module _1_bit_AU (
  input  Cin,
  input  A,
  input  B,
  input  [1:0] S1S0,
  output D,
  output Cout
);

  wire multiplexer_1_out, not_1_out;

  not not_1 (not_1_out, B);
  Multiplexer #(.select(2), .enable("false")) multiplexer_1 (
    .in0(B), .in1(not_1_out), .in2(1'b0), .in3(1'b1), .out(multiplexer_1_out), .sel(S1S0));
  Adder #(.width(1)) adder_1 (.a(A), .b(multiplexer_1_out), .out(D), .cin(Cin), .cout(Cout));

  // Notes on the sheet:
  //   1-bit Arithmetic Unit
endmodule

module _2_bit_AU (
  input  Cin,
  input  [1:0] A1A0,
  input  [1:0] B1B0,
  input  [1:0] S1S0,
  output [1:0] D1D0,
  output Cout
);

  wire _0_cout;

  _1_bit_AU _0 (.Cin(Cin), .A(A1A0[0]), .B(B1B0[0]), .S1S0(S1S0), .D(D1D0[0]), .Cout(_0_cout));
  _1_bit_AU _1 (.Cin(_0_cout), .A(A1A0[1]), .B(B1B0[1]), .S1S0(S1S0), .D(D1D0[1]), .Cout(Cout));

  // Notes on the sheet:
  //   2-bit Arithmetic Unit
endmodule

module _8_bit_AU (
  input  Cin,
  input  [7:0] A7_A0,
  input  [7:0] B7_B0,
  input  [1:0] S1S0,
  output [7:0] D7_D0,
  output Cout
);

  wire _0_1_cout, _2_3_cout, _4_5_cout;

  _2_bit_AU _0_1 (.Cin(Cin), .A1A0(A7_A0[1:0]), .B1B0(B7_B0[1:0]), .S1S0(S1S0), .D1D0(D7_D0[1:0]), .Cout(_0_1_cout));
  _2_bit_AU _2_3 (
    .Cin(_0_1_cout), .A1A0(A7_A0[3:2]), .B1B0(B7_B0[3:2]), .S1S0(S1S0), .D1D0(D7_D0[3:2]), .Cout(_2_3_cout));
  _2_bit_AU _4_5 (
    .Cin(_2_3_cout), .A1A0(A7_A0[5:4]), .B1B0(B7_B0[5:4]), .S1S0(S1S0), .D1D0(D7_D0[5:4]), .Cout(_4_5_cout));
  _2_bit_AU _6_7 (.Cin(_4_5_cout), .A1A0(A7_A0[7:6]), .B1B0(B7_B0[7:6]), .S1S0(S1S0), .D1D0(D7_D0[7:6]), .Cout(Cout));

  // Notes on the sheet:
  //   8-bit Arithmetic Unit
endmodule

module _32_bit_Arithmetic_Unit (
  input  Cin,
  input  [31:0] A31_A0,
  input  [31:0] B31_B0,
  input  [1:0] S1S0,
  output [31:0] D31_D0,
  output Cout
);

  wire _0_7_cout, _8_15_cout, _16_23_cout;

  _8_bit_AU _0_7 (
    .Cin(Cin), .A7_A0(A31_A0[7:0]), .B7_B0(B31_B0[7:0]), .S1S0(S1S0), .D7_D0(D31_D0[7:0]), .Cout(_0_7_cout));
  _8_bit_AU _8_15 (
    .Cin(_0_7_cout), .A7_A0(A31_A0[15:8]), .B7_B0(B31_B0[15:8]), .S1S0(S1S0), .D7_D0(D31_D0[15:8]),
    .Cout(_8_15_cout));
  _8_bit_AU _16_23 (
    .Cin(_8_15_cout), .A7_A0(A31_A0[23:16]), .B7_B0(B31_B0[23:16]), .S1S0(S1S0), .D7_D0(D31_D0[23:16]),
    .Cout(_16_23_cout));
  _8_bit_AU _24_31 (
    .Cin(_16_23_cout), .A7_A0(A31_A0[31:24]), .B7_B0(B31_B0[31:24]), .S1S0(S1S0), .D7_D0(D31_D0[31:24]),
    .Cout(Cout));

  // Notes on the sheet:
  //   32-bit Arithmetic Unit
  //   Md. Rifat Ahmed
  //   ID: 1931725042
endmodule

module _2_bit_X_2_bit (
  input  [1:0] B,
  input  [1:0] A,
  input  Cin,
  output [3:0] Product
);

  wire [0:0] A0B1_out;
  wire [1:0] A1B0_out;

  and A1B1 (A1B0_out[1], A[1], B[1]);
  and A1B0 (A1B0_out[0], A[1], B[0]);
  and A0B1 (A0B1_out[0], A[0], B[1]);
  and A0B0 (Product[0], A[0], B[0]);
  Adder #(.width(2)) adder_1 (.a({1'b0, A0B1_out[0]}), .b(A1B0_out), .out(Product[2:1]), .cin(Cin), .cout(Product[3]));
endmodule

module _4_bit_X_4_bit (
  input  [3:0] B,
  input  [3:0] A,
  output [7:0] P
);

  wire [2:0] and_15_out;
  wire [3:0] adder_1_out, adder_2_out, and_4_out, and_9_out, and_12_out;

  and and_1 (and_4_out[3], B[3], A[3]);
  and and_2 (and_4_out[2], B[2], A[3]);
  and and_3 (and_4_out[1], B[1], A[3]);
  and and_4 (and_4_out[0], B[0], A[3]);
  and and_5 (and_9_out[2], B[2], A[2]);
  and and_6 (and_9_out[3], B[3], A[2]);
  and and_7 (and_9_out[1], B[1], A[2]);
  and and_8 (and_12_out[3], B[3], A[1]);
  and and_9 (and_9_out[0], B[0], A[2]);
  and and_10 (and_12_out[2], B[2], A[1]);
  and and_11 (and_12_out[1], B[1], A[1]);
  and and_12 (and_12_out[0], B[0], A[1]);
  and and_13 (and_15_out[1], B[2], A[0]);
  and and_14 (and_15_out[2], B[3], A[0]);
  and and_15 (and_15_out[0], B[1], A[0]);
  Adder #(.width(4)) adder_1 (
    .a({1'b0, and_15_out}), .b(and_12_out), .out({adder_1_out[2:0], P[1]}), .cin(1'b0), .cout(adder_1_out[3]));
  and and_16 (P[0], B[0], A[0]);
  Adder #(.width(4)) adder_2 (
    .a(adder_1_out), .b(and_9_out), .out({adder_2_out[2:0], P[2]}), .cin(1'b0), .cout(adder_2_out[3]));
  Adder #(.width(4)) adder_3 (.a(adder_2_out), .b(and_4_out), .out(P[6:3]), .cin(1'b0), .cout(P[7]));

  // Notes on the sheet:
  //   4-bit X 4-bit Multiplication Unit
endmodule

// B14
module _16_bit_X_16_bit (
  input  [15:0] A,
  input  [15:0] B,
  output [31:0] P
);

  wire [14:0] A0;
  wire [15:0] A1, A2, A3, A4, A5, A6, A7, A8, A9, A10, A11, A12, A13, A14, A15, adder_1_out, adder_2_out,
       adder_3_cout, adder_4_out, adder_5_out, adder_6_out, adder_7_out, adder_8_out, adder_9_out,
       adder_10_out, adder_11_cout, adder_12_out, adder_13_out, adder_14_out;

  and and_1 (A15[15], B[15], A[15]);
  and and_2 (A13[15], B[15], A[13]);
  and and_3 (A14[14], B[14], A[14]);
  and and_4 (A14[15], B[15], A[14]);
  and and_5 (A15[14], B[14], A[15]);
  and and_6 (A15[13], B[13], A[15]);
  and and_7 (A11[15], B[15], A[11]);
  and and_8 (A12[14], B[14], A[12]);
  and and_9 (A12[15], B[15], A[12]);
  and and_10 (A13[13], B[13], A[13]);
  and and_11 (A13[14], B[14], A[13]);
  and and_12 (A14[13], B[13], A[14]);
  and and_13 (A14[12], B[12], A[14]);
  and and_14 (A15[11], B[11], A[15]);
  and and_15 (A15[12], B[12], A[15]);
  and and_16 (A9[15], B[15], A[9]);
  and and_17 (A10[14], B[14], A[10]);
  and and_18 (A10[15], B[15], A[10]);
  and and_19 (A11[13], B[13], A[11]);
  and and_20 (A11[14], B[14], A[11]);
  and and_21 (A12[12], B[12], A[12]);
  and and_22 (A12[13], B[13], A[12]);
  and and_23 (A13[12], B[12], A[13]);
  and and_24 (A13[11], B[11], A[13]);
  and and_25 (A14[10], B[10], A[14]);
  and and_26 (A14[11], B[11], A[14]);
  and and_27 (A15[9], B[9], A[15]);
  and and_28 (A15[10], B[10], A[15]);
  and and_29 (A8[14], B[14], A[8]);
  and and_30 (A8[15], B[15], A[8]);
  and and_31 (A9[13], B[13], A[9]);
  and and_32 (A9[14], B[14], A[9]);
  and and_33 (A10[13], B[13], A[10]);
  and and_34 (A10[12], B[12], A[10]);
  and and_35 (A11[12], B[12], A[11]);
  and and_36 (A11[11], B[11], A[11]);
  and and_37 (A12[11], B[11], A[12]);
  and and_38 (A12[10], B[10], A[12]);
  and and_39 (A13[10], B[10], A[13]);
  and and_40 (A13[9], B[9], A[13]);
  and and_41 (A14[8], B[8], A[14]);
  and and_42 (A14[9], B[9], A[14]);
  and and_43 (A15[7], B[7], A[15]);
  and and_44 (A15[8], B[8], A[15]);
  and and_45 (A8[13], B[13], A[8]);
  and and_46 (A8[12], B[12], A[8]);
  and and_47 (A9[11], B[11], A[9]);
  and and_48 (A9[12], B[12], A[9]);
  and and_49 (A10[10], B[10], A[10]);
  and and_50 (A10[11], B[11], A[10]);
  and and_51 (A11[9], B[9], A[11]);
  and and_52 (A11[10], B[10], A[11]);
  and and_53 (A12[9], B[9], A[12]);
  and and_54 (A12[8], B[8], A[12]);
  and and_55 (A13[8], B[8], A[13]);
  and and_56 (A13[7], B[7], A[13]);
  and and_57 (A14[6], B[6], A[14]);
  and and_58 (A14[7], B[7], A[14]);
  and and_59 (A15[6], B[6], A[15]);
  and and_60 (A15[5], B[5], A[15]);
  and and_61 (A8[11], B[11], A[8]);
  and and_62 (A8[10], B[10], A[8]);
  and and_63 (A9[10], B[10], A[9]);
  and and_64 (A9[9], B[9], A[9]);
  and and_65 (A10[8], B[8], A[10]);
  and and_66 (A10[9], B[9], A[10]);
  and and_67 (A11[8], B[8], A[11]);
  and and_68 (A11[7], B[7], A[11]);
  and and_69 (A12[6], B[6], A[12]);
  and and_70 (A12[7], B[7], A[12]);
  and and_71 (A13[5], B[5], A[13]);
  and and_72 (A13[6], B[6], A[13]);
  and and_73 (A14[5], B[5], A[14]);
  and and_74 (A14[4], B[4], A[14]);
  and and_75 (A15[3], B[3], A[15]);
  and and_76 (A15[4], B[4], A[15]);
  and and_77 (A8[8], B[8], A[8]);
  and and_78 (A8[9], B[9], A[8]);
  and and_79 (A9[7], B[7], A[9]);
  and and_80 (A9[8], B[8], A[9]);
  and and_81 (A10[6], B[6], A[10]);
  and and_82 (A10[7], B[7], A[10]);
  and and_83 (A11[5], B[5], A[11]);
  and and_84 (A11[6], B[6], A[11]);
  and and_85 (A12[4], B[4], A[12]);
  and and_86 (A12[5], B[5], A[12]);
  and and_87 (A13[3], B[3], A[13]);
  and and_88 (A13[4], B[4], A[13]);
  and and_89 (A14[3], B[3], A[14]);
  and and_90 (A14[2], B[2], A[14]);
  and and_91 (A15[2], B[2], A[15]);
  and and_92 (A15[1], B[1], A[15]);
  and and_93 (A8[7], B[7], A[8]);
  and and_94 (A8[6], B[6], A[8]);
  and and_95 (A9[6], B[6], A[9]);
  and and_96 (A9[5], B[5], A[9]);
  and and_97 (A10[4], B[4], A[10]);
  and and_98 (A10[5], B[5], A[10]);
  and and_99 (A11[3], B[3], A[11]);
  and and_100 (A11[4], B[4], A[11]);
  and and_101 (A12[3], B[3], A[12]);
  and and_102 (A12[2], B[2], A[12]);
  and and_103 (A13[1], B[1], A[13]);
  and and_104 (A13[2], B[2], A[13]);
  and and_105 (A14[1], B[1], A[14]);
  and and_106 (A14[0], B[0], A[14]);
  and and_107 (A15[0], B[0], A[15]);
  and and_108 (A8[5], B[5], A[8]);
  and and_109 (A8[4], B[4], A[8]);
  and and_110 (A9[3], B[3], A[9]);
  and and_111 (A9[4], B[4], A[9]);
  and and_112 (A10[2], B[2], A[10]);
  and and_113 (A10[3], B[3], A[10]);
  and and_114 (A11[2], B[2], A[11]);
  and and_115 (A11[1], B[1], A[11]);
  and and_116 (A12[1], B[1], A[12]);
  and and_117 (A12[0], B[0], A[12]);
  and and_118 (A13[0], B[0], A[13]);
  and and_119 (A8[2], B[2], A[8]);
  and and_120 (A8[3], B[3], A[8]);
  and and_121 (A9[2], B[2], A[9]);
  and and_122 (A9[1], B[1], A[9]);
  and and_123 (A10[0], B[0], A[10]);
  and and_124 (A10[1], B[1], A[10]);
  and and_125 (A11[0], B[0], A[11]);
  and and_126 (A8[1], B[1], A[8]);
  and and_127 (A8[0], B[0], A[8]);
  and and_128 (A9[0], B[0], A[9]);
  and and_129 (A6[15], B[15], A[6]);
  and and_130 (A7[15], B[15], A[7]);
  and and_131 (A7[14], B[14], A[7]);
  and and_132 (A4[15], B[15], A[4]);
  and and_133 (A5[15], B[15], A[5]);
  and and_134 (A5[14], B[14], A[5]);
  and and_135 (A6[13], B[13], A[6]);
  and and_136 (A6[14], B[14], A[6]);
  and and_137 (A7[13], B[13], A[7]);
  and and_138 (A7[12], B[12], A[7]);
  and and_139 (A2[15], B[15], A[2]);
  and and_140 (A3[15], B[15], A[3]);
  and and_141 (A3[14], B[14], A[3]);
  and and_142 (A4[13], B[13], A[4]);
  and and_143 (A4[14], B[14], A[4]);
  and and_144 (A5[13], B[13], A[5]);
  and and_145 (A5[12], B[12], A[5]);
  and and_146 (A6[11], B[11], A[6]);
  and and_147 (A6[12], B[12], A[6]);
  and and_148 (A7[11], B[11], A[7]);
  and and_149 (A7[10], B[10], A[7]);
  and and_150 (A0[14], B[15], A[0]);
  and and_151 (A1[15], B[15], A[1]);
  and and_152 (A1[14], B[14], A[1]);
  and and_153 (A2[14], B[14], A[2]);
  and and_154 (A2[13], B[13], A[2]);
  and and_155 (A3[12], B[12], A[3]);
  and and_156 (A3[13], B[13], A[3]);
  and and_157 (A4[12], B[12], A[4]);
  and and_158 (A4[11], B[11], A[4]);
  and and_159 (A5[11], B[11], A[5]);
  and and_160 (A5[10], B[10], A[5]);
  and and_161 (A6[10], B[10], A[6]);
  and and_162 (A6[9], B[9], A[6]);
  and and_163 (A7[8], B[8], A[7]);
  and and_164 (A7[9], B[9], A[7]);
  and and_165 (A0[13], B[14], A[0]);
  and and_166 (A0[12], B[13], A[0]);
  and and_167 (A1[12], B[12], A[1]);
  and and_168 (A1[13], B[13], A[1]);
  and and_169 (A2[12], B[12], A[2]);
  and and_170 (A2[11], B[11], A[2]);
  and and_171 (A3[10], B[10], A[3]);
  and and_172 (A3[11], B[11], A[3]);
  and and_173 (A4[10], B[10], A[4]);
  and and_174 (A4[9], B[9], A[4]);
  and and_175 (A5[9], B[9], A[5]);
  and and_176 (A5[8], B[8], A[5]);
  and and_177 (A6[8], B[8], A[6]);
  and and_178 (A6[7], B[7], A[6]);
  and and_179 (A7[7], B[7], A[7]);
  and and_180 (A7[6], B[6], A[7]);
  and and_181 (A0[10], B[11], A[0]);
  and and_182 (A0[11], B[12], A[0]);
  and and_183 (A1[11], B[11], A[1]);
  and and_184 (A1[10], B[10], A[1]);
  and and_185 (A2[9], B[9], A[2]);
  and and_186 (A2[10], B[10], A[2]);
  and and_187 (A3[8], B[8], A[3]);
  and and_188 (A3[9], B[9], A[3]);
  and and_189 (A4[7], B[7], A[4]);
  and and_190 (A4[8], B[8], A[4]);
  and and_191 (A5[6], B[6], A[5]);
  and and_192 (A5[7], B[7], A[5]);
  and and_193 (A6[5], B[5], A[6]);
  and and_194 (A6[6], B[6], A[6]);
  and and_195 (A7[5], B[5], A[7]);
  and and_196 (A7[4], B[4], A[7]);
  and and_197 (A0[8], B[9], A[0]);
  and and_198 (A0[9], B[10], A[0]);
  and and_199 (A1[9], B[9], A[1]);
  and and_200 (A1[8], B[8], A[1]);
  and and_201 (A2[8], B[8], A[2]);
  and and_202 (A2[7], B[7], A[2]);
  and and_203 (A3[6], B[6], A[3]);
  and and_204 (A3[7], B[7], A[3]);
  and and_205 (A4[5], B[5], A[4]);
  and and_206 (A4[6], B[6], A[4]);
  and and_207 (A5[4], B[4], A[5]);
  and and_208 (A5[5], B[5], A[5]);
  and and_209 (A6[4], B[4], A[6]);
  and and_210 (A6[3], B[3], A[6]);
  and and_211 (A7[2], B[2], A[7]);
  and and_212 (A7[3], B[3], A[7]);
  and and_213 (A0[7], B[8], A[0]);
  and and_214 (A0[6], B[7], A[0]);
  and and_215 (A1[6], B[6], A[1]);
  and and_216 (A1[7], B[7], A[1]);
  and and_217 (A2[5], B[5], A[2]);
  and and_218 (A2[6], B[6], A[2]);
  and and_219 (A3[4], B[4], A[3]);
  and and_220 (A3[5], B[5], A[3]);
  and and_221 (A4[4], B[4], A[4]);
  and and_222 (A4[3], B[3], A[4]);
  and and_223 (A5[3], B[3], A[5]);
  and and_224 (A5[2], B[2], A[5]);
  and and_225 (A6[1], B[1], A[6]);
  and and_226 (A6[2], B[2], A[6]);
  and and_227 (A7[1], B[1], A[7]);
  and and_228 (A7[0], B[0], A[7]);
  and and_229 (A0[4], B[5], A[0]);
  and and_230 (A0[5], B[6], A[0]);
  and and_231 (A1[4], B[4], A[1]);
  and and_232 (A1[5], B[5], A[1]);
  and and_233 (A2[4], B[4], A[2]);
  and and_234 (A2[3], B[3], A[2]);
  and and_235 (A3[3], B[3], A[3]);
  and and_236 (A3[2], B[2], A[3]);
  and and_237 (A4[2], B[2], A[4]);
  and and_238 (A4[1], B[1], A[4]);
  and and_239 (A5[1], B[1], A[5]);
  and and_240 (A5[0], B[0], A[5]);
  and and_241 (A6[0], B[0], A[6]);
  and and_242 (A0[2], B[3], A[0]);
  and and_243 (A0[3], B[4], A[0]);
  and and_244 (A1[2], B[2], A[1]);
  and and_245 (A1[3], B[3], A[1]);
  and and_246 (A2[2], B[2], A[2]);
  and and_247 (A2[1], B[1], A[2]);
  and and_248 (A3[1], B[1], A[3]);
  and and_249 (A3[0], B[0], A[3]);
  and and_250 (A4[0], B[0], A[4]);
  and and_251 (A0[1], B[2], A[0]);
  and and_252 (A0[0], B[1], A[0]);
  and and_253 (A1[0], B[0], A[1]);
  and and_254 (A1[1], B[1], A[1]);
  and and_255 (A2[0], B[0], A[2]);
  and and_256 (P[0], B[0], A[0]);
  Adder #(.width(16)) adder_1 (
    .a({1'b0, A0}), .b(A1), .out({adder_1_out[14:0], P[1]}), .cin(1'b0), .cout(adder_1_out[15]));
  Adder #(.width(16)) adder_2 (
    .a(adder_1_out), .b(A2), .out({adder_2_out[14:0], P[2]}), .cin(1'b0), .cout(adder_2_out[15]));
  Adder #(.width(16)) adder_3 (
    .a(adder_2_out), .b(A3), .out({adder_3_cout[14:0], P[3]}), .cin(1'b0), .cout(adder_3_cout[15]));
  Adder #(.width(16)) adder_4 (
    .a(adder_3_cout), .b(A4), .out({adder_4_out[14:0], P[4]}), .cin(1'b0), .cout(adder_4_out[15]));
  Adder #(.width(16)) adder_5 (
    .a(adder_4_out), .b(A5), .out({adder_5_out[14:0], P[5]}), .cin(1'b0), .cout(adder_5_out[15]));
  Adder #(.width(16)) adder_6 (
    .a(adder_5_out), .b(A6), .out({adder_6_out[14:0], P[6]}), .cin(1'b0), .cout(adder_6_out[15]));
  Adder #(.width(16)) adder_7 (
    .a(adder_6_out), .b(A7), .out({adder_7_out[14:0], P[7]}), .cin(1'b0), .cout(adder_7_out[15]));
  Adder #(.width(16)) adder_8 (
    .a(adder_7_out), .b(A8), .out({adder_8_out[14:0], P[8]}), .cin(1'b0), .cout(adder_8_out[15]));
  Adder #(.width(16)) adder_9 (
    .a(adder_8_out), .b(A9), .out({adder_9_out[14:0], P[9]}), .cin(1'b0), .cout(adder_9_out[15]));
  Adder #(.width(16)) adder_10 (
    .a(adder_9_out), .b(A10), .out({adder_10_out[14:0], P[10]}), .cin(1'b0), .cout(adder_10_out[15]));
  Adder #(.width(16)) adder_11 (
    .a(adder_10_out), .b(A11), .out({adder_11_cout[14:0], P[11]}), .cin(1'b0), .cout(adder_11_cout[15]));
  Adder #(.width(16)) adder_12 (
    .a(adder_11_cout), .b(A12), .out({adder_12_out[14:0], P[12]}), .cin(1'b0), .cout(adder_12_out[15]));
  Adder #(.width(16)) adder_13 (
    .a(adder_12_out), .b(A13), .out({adder_13_out[14:0], P[13]}), .cin(1'b0), .cout(adder_13_out[15]));
  Adder #(.width(16)) adder_14 (
    .a(adder_13_out), .b(A14), .out({adder_14_out[14:0], P[14]}), .cin(1'b0), .cout(adder_14_out[15]));
  Adder #(.width(16)) adder_15 (.a(adder_14_out), .b(A15), .out(P[30:15]), .cin(1'b0), .cout(P[31]));

  // Notes on the sheet:
  //   16-bit X 16-bit Multiplication Unit
  //   Md. Rifat Ahmed
  //   ID: 1931725042
endmodule
