// Logisim project CSE332.9-1931725042-Md. Rifat Ahmed-LAB HW 4-ALU Control.circ as structural Verilog
module _1_bit_LU (
  input  A,
  input  B,
  input  [1:0] S1S0,
  output F
);

  wire and_1_out, not_1_out, or_1_out, xor_1_out;

  and and_1 (and_1_out, A, B);
  or or_1 (or_1_out, A, B);
  xor xor_1 (xor_1_out, A, B);
  not not_1 (not_1_out, A);
  Multiplexer #(.select(2)) multiplexer_1 (
    .in0(and_1_out), .in1(or_1_out), .in2(xor_1_out), .in3(not_1_out), .out(F), .sel(S1S0));  // open: en

  // Notes on the sheet:
  //   1-bit Logic Unit
endmodule

module _2_bit_LU (
  input  [1:0] A,
  input  [1:0] B,
  input  [1:0] S1S0,
  output [1:0] F
);

  _1_bit_LU _0 (.A(A[0]), .B(B[0]), .S1S0(S1S0), .F(F[0]));
  _1_bit_LU _1 (.A(A[1]), .B(B[1]), .S1S0(S1S0), .F(F[1]));

  // Notes on the sheet:
  //   A0
  //   A1
  //   B0
  //   B1
  //   2-bit Logic Unit
endmodule

module _8_bit_LU (
  input  [7:0] A,
  input  [7:0] B,
  input  [1:0] S1S0,
  output [7:0] F
);

  _2_bit_LU _0_1 (.A(A[1:0]), .B(B[1:0]), .S1S0(S1S0), .F(F[1:0]));
  _2_bit_LU _2_3 (.A(A[3:2]), .B(B[3:2]), .S1S0(S1S0), .F(F[3:2]));
  _2_bit_LU _4_5 (.A(A[5:4]), .B(B[5:4]), .S1S0(S1S0), .F(F[5:4]));
  _2_bit_LU _6_7 (.A(A[7:6]), .B(B[7:6]), .S1S0(S1S0), .F(F[7:6]));

  // Notes on the sheet:
  //   8-bit Logic Unit
endmodule

// 32-bit LU
module _32_bit_Logic_Unit (
  input  [31:0] A,
  input  [31:0] B,
  input  [1:0] S1S0,
  output [31:0] F
);

  _8_bit_LU u_8_bit_lu_1 (.A(A[7:0]), .B(B[7:0]), .S1S0(S1S0), .F(F[7:0]));
  _8_bit_LU u_8_bit_lu_2 (.A(A[15:8]), .B(B[15:8]), .S1S0(S1S0), .F(F[15:8]));
  _8_bit_LU u_8_bit_lu_3 (.A(A[23:16]), .B(B[23:16]), .S1S0(S1S0), .F(F[23:16]));
  _8_bit_LU u_8_bit_lu_4 (.A(A[31:24]), .B(B[31:24]), .S1S0(S1S0), .F(F[31:24]));

  // Notes on the sheet:
  //   32-bit Logic Unit
  //   Md. Rifat Ahmed
  //   ID: 1931725042
endmodule

module _1_bit_AU (
  input  Cin,
  input  A,
  input  B,
  input  [1:0] S1S0,
  output D,
  output Cout
);

  wire multiplexer_1_out, not_1_out;

  not not_1 (not_1_out, B);
  Multiplexer #(.select(2), .enable("false")) multiplexer_1 (
    .in0(B), .in1(not_1_out), .in2(1'b0), .in3(1'b1), .out(multiplexer_1_out), .sel(S1S0));
  Adder #(.width(1)) adder_1 (.a(A), .b(multiplexer_1_out), .out(D), .cin(Cin), .cout(Cout));

  // Notes on the sheet:
  //   1-bit Arithmetic Unit
endmodule

module _2_bit_AU (
  input  Cin,
  input  [1:0] A1A0,
  input  [1:0] B1B0,
  input  [1:0] S1S0,
  output [1:0] D1D0,
  output Cout
);

  wire _0_cout;

  _1_bit_AU _0 (.Cin(Cin), .A(A1A0[0]), .B(B1B0[0]), .S1S0(S1S0), .D(D1D0[0]), .Cout(_0_cout));
  _1_bit_AU _1 (.Cin(_0_cout), .A(A1A0[1]), .B(B1B0[1]), .S1S0(S1S0), .D(D1D0[1]), .Cout(Cout));

  // Notes on the sheet:
  //   2-bit Arithmetic Unit
endmodule

module _8_bit_AU (
  input  Cin,
  input  [7:0] A7_A0,
  input  [7:0] B7_B0,
  input  [1:0] S1S0,
  output [7:0] D7_D0,
  output Cout
);

  wire _0_1_cout, _2_3_cout, _4_5_cout;

  _2_bit_AU _0_1 (.Cin(Cin), .A1A0(A7_A0[1:0]), .B1B0(B7_B0[1:0]), .S1S0(S1S0), .D1D0(D7_D0[1:0]), .Cout(_0_1_cout));
  _2_bit_AU _2_3 (
    .Cin(_0_1_cout), .A1A0(A7_A0[3:2]), .B1B0(B7_B0[3:2]), .S1S0(S1S0), .D1D0(D7_D0[3:2]), .Cout(_2_3_cout));
  _2_bit_AU _4_5 (
    .Cin(_2_3_cout), .A1A0(A7_A0[5:4]), .B1B0(B7_B0[5:4]), .S1S0(S1S0), .D1D0(D7_D0[5:4]), .Cout(_4_5_cout));
  _2_bit_AU _6_7 (.Cin(_4_5_cout), .A1A0(A7_A0[7:6]), .B1B0(B7_B0[7:6]), .S1S0(S1S0), .D1D0(D7_D0[7:6]), .Cout(Cout));

  // Notes on the sheet:
  //   8-bit Arithmetic Unit
endmodule

module _32_bit_Arithmetic_Unit (
  input  Cin,
  input  [31:0] A31_A0,
  input  [31:0] B31_B0,
  input  [1:0] S1S0,
  output [31:0] D31_D0,
  output Cout
);

  wire _0_7_cout, _8_15_cout, _16_23_cout;

  _8_bit_AU _0_7 (
    .Cin(Cin), .A7_A0(A31_A0[7:0]), .B7_B0(B31_B0[7:0]), .S1S0(S1S0), .D7_D0(D31_D0[7:0]), .Cout(_0_7_cout));
  _8_bit_AU _8_15 (
    .Cin(_0_7_cout), .A7_A0(A31_A0[15:8]), .B7_B0(B31_B0[15:8]), .S1S0(S1S0), .D7_D0(D31_D0[15:8]),
    .Cout(_8_15_cout));
  _8_bit_AU _16_23 (
    .Cin(_8_15_cout), .A7_A0(A31_A0[23:16]), .B7_B0(B31_B0[23:16]), .S1S0(S1S0), .D7_D0(D31_D0[23:16]),
    .Cout(_16_23_cout));
  _8_bit_AU _24_31 (
    .Cin(_16_23_cout), .A7_A0(A31_A0[31:24]), .B7_B0(B31_B0[31:24]), .S1S0(S1S0), .D7_D0(D31_D0[31:24]),
    .Cout(Cout));

  // Notes on the sheet:
  //   32-bit Arithmetic Unit
  //   Md. Rifat Ahmed
  //   ID: 1931725042
endmodule

module _2_bit_X_2_bit (
  input  [1:0] B,
  input  [1:0] A,
  input  Cin,
  output [3:0] Product
);

  wire [0:0] A0B1_out;
  wire [1:0] A1B0_out;

  and A1B1 (A1B0_out[1], A[1], B[1]);
  and A1B0 (A1B0_out[0], A[1], B[0]);
  and A0B1 (A0B1_out[0], A[0], B[1]);
  and A0B0 (Product[0], A[0], B[0]);
  Adder #(.width(2)) adder_1 (.a({1'b0, A0B1_out[0]}), .b(A1B0_out), .out(Product[2:1]), .cin(Cin), .cout(Product[3]));
endmodule

module _4_bit_X_4_bit (
  input  [3:0] B,
  input  [3:0] A,
  output [7:0] P
);

  wire [2:0] and_15_out;
  wire [3:0] adder_1_out, adder_2_out, and_3_out, and_9_out, and_11_out;

  and and_1 (and_3_out[3], B[3], A[3]);
  and and_2 (and_3_out[2], B[2], A[3]);
  and and_3 (and_3_out[0], B[0], A[3]);
  and and_4 (and_3_out[1], B[1], A[3]);
  and and_5 (and_9_out[2], B[2], A[2]);
  and and_6 (and_9_out[3], B[3], A[2]);
  and and_7 (and_9_out[1], B[1], A[2]);
  and and_8 (and_11_out[3], B[3], A[1]);
  and and_9 (and_9_out[0], B[0], A[2]);
  and and_10 (and_11_out[2], B[2], A[1]);
  and and_11 (and_11_out[0], B[0], A[1]);
  and and_12 (and_11_out[1], B[1], A[1]);
  and and_13 (and_15_out[1], B[2], A[0]);
  and and_14 (and_15_out[2], B[3], A[0]);
  and and_15 (and_15_out[0], B[1], A[0]);
  Adder #(.width(4)) adder_1 (
    .a({1'b0, and_15_out}), .b(and_11_out), .out({adder_1_out[2:0], P[1]}), .cin(1'b0), .cout(adder_1_out[3]));
  and and_16 (P[0], B[0], A[0]);
  Adder #(.width(4)) adder_2 (
    .a(adder_1_out), .b(and_9_out), .out({adder_2_out[2:0], P[2]}), .cin(1'b0), .cout(adder_2_out[3]));
  Adder #(.width(4)) adder_3 (.a(adder_2_out), .b(and_3_out), .out(P[6:3]), .cin(1'b0), .cout(P[7]));

  // Notes on the sheet:
  //   4-bit X 4-bit Multiplication Unit
endmodule

// Multiplier
module _32_bit_Multiplier (
  input  [15:0] A,
  input  [15:0] B,
  output [31:0] P
);

  wire [14:0] A0;
  wire [15:0] A1, A2, A3, A4, A5, A6, A7, A8, A9, A10, A11, A12, A13, A14, A15, adder_1_out, adder_2_out,
       adder_3_cout, adder_4_out, adder_5_out, adder_6_out, adder_7_out, adder_8_out, adder_9_out,
       adder_10_out, adder_11_cout, adder_12_out, adder_13_out, adder_14_out;

  and and_1 (A15[15], B[15], A[15]);
  and and_2 (A13[15], B[15], A[13]);
  and and_3 (A14[15], B[15], A[14]);
  and and_4 (A14[14], B[14], A[14]);
  and and_5 (A15[13], B[13], A[15]);
  and and_6 (A15[14], B[14], A[15]);
  and and_7 (A11[15], B[15], A[11]);
  and and_8 (A12[14], B[14], A[12]);
  and and_9 (A12[15], B[15], A[12]);
  and and_10 (A13[14], B[14], A[13]);
  and and_11 (A13[13], B[13], A[13]);
  and and_12 (A14[13], B[13], A[14]);
  and and_13 (A14[12], B[12], A[14]);
  and and_14 (A15[11], B[11], A[15]);
  and and_15 (A15[12], B[12], A[15]);
  and and_16 (A9[15], B[15], A[9]);
  and and_17 (A10[14], B[14], A[10]);
  and and_18 (A10[15], B[15], A[10]);
  and and_19 (A11[13], B[13], A[11]);
  and and_20 (A11[14], B[14], A[11]);
  and and_21 (A12[13], B[13], A[12]);
  and and_22 (A12[12], B[12], A[12]);
  and and_23 (A13[11], B[11], A[13]);
  and and_24 (A13[12], B[12], A[13]);
  and and_25 (A14[10], B[10], A[14]);
  and and_26 (A14[11], B[11], A[14]);
  and and_27 (A15[9], B[9], A[15]);
  and and_28 (A15[10], B[10], A[15]);
  and and_29 (A8[14], B[14], A[8]);
  and and_30 (A8[15], B[15], A[8]);
  and and_31 (A9[13], B[13], A[9]);
  and and_32 (A9[14], B[14], A[9]);
  and and_33 (A10[13], B[13], A[10]);
  and and_34 (A10[12], B[12], A[10]);
  and and_35 (A11[11], B[11], A[11]);
  and and_36 (A11[12], B[12], A[11]);
  and and_37 (A12[11], B[11], A[12]);
  and and_38 (A12[10], B[10], A[12]);
  and and_39 (A13[9], B[9], A[13]);
  and and_40 (A13[10], B[10], A[13]);
  and and_41 (A14[9], B[9], A[14]);
  and and_42 (A14[8], B[8], A[14]);
  and and_43 (A15[7], B[7], A[15]);
  and and_44 (A15[8], B[8], A[15]);
  and and_45 (A8[12], B[12], A[8]);
  and and_46 (A8[13], B[13], A[8]);
  and and_47 (A9[11], B[11], A[9]);
  and and_48 (A9[12], B[12], A[9]);
  and and_49 (A10[11], B[11], A[10]);
  and and_50 (A10[10], B[10], A[10]);
  and and_51 (A11[10], B[10], A[11]);
  and and_52 (A11[9], B[9], A[11]);
  and and_53 (A12[8], B[8], A[12]);
  and and_54 (A12[9], B[9], A[12]);
  and and_55 (A13[8], B[8], A[13]);
  and and_56 (A13[7], B[7], A[13]);
  and and_57 (A14[6], B[6], A[14]);
  and and_58 (A14[7], B[7], A[14]);
  and and_59 (A15[6], B[6], A[15]);
  and and_60 (A15[5], B[5], A[15]);
  and and_61 (A8[11], B[11], A[8]);
  and and_62 (A8[10], B[10], A[8]);
  and and_63 (A9[9], B[9], A[9]);
  and and_64 (A9[10], B[10], A[9]);
  and and_65 (A10[9], B[9], A[10]);
  and and_66 (A10[8], B[8], A[10]);
  and and_67 (A11[7], B[7], A[11]);
  and and_68 (A11[8], B[8], A[11]);
  and and_69 (A12[7], B[7], A[12]);
  and and_70 (A12[6], B[6], A[12]);
  and and_71 (A13[5], B[5], A[13]);
  and and_72 (A13[6], B[6], A[13]);
  and and_73 (A14[5], B[5], A[14]);
  and and_74 (A14[4], B[4], A[14]);
  and and_75 (A15[4], B[4], A[15]);
  and and_76 (A15[3], B[3], A[15]);
  and and_77 (A8[9], B[9], A[8]);
  and and_78 (A8[8], B[8], A[8]);
  and and_79 (A9[7], B[7], A[9]);
  and and_80 (A9[8], B[8], A[9]);
  and and_81 (A10[6], B[6], A[10]);
  and and_82 (A10[7], B[7], A[10]);
  and and_83 (A11[5], B[5], A[11]);
  and and_84 (A11[6], B[6], A[11]);
  and and_85 (A12[5], B[5], A[12]);
  and and_86 (A12[4], B[4], A[12]);
  and and_87 (A13[4], B[4], A[13]);
  and and_88 (A13[3], B[3], A[13]);
  and and_89 (A14[2], B[2], A[14]);
  and and_90 (A14[3], B[3], A[14]);
  and and_91 (A15[1], B[1], A[15]);
  and and_92 (A15[2], B[2], A[15]);
  and and_93 (A8[7], B[7], A[8]);
  and and_94 (A8[6], B[6], A[8]);
  and and_95 (A9[5], B[5], A[9]);
  and and_96 (A9[6], B[6], A[9]);
  and and_97 (A10[5], B[5], A[10]);
  and and_98 (A10[4], B[4], A[10]);
  and and_99 (A11[3], B[3], A[11]);
  and and_100 (A11[4], B[4], A[11]);
  and and_101 (A12[2], B[2], A[12]);
  and and_102 (A12[3], B[3], A[12]);
  and and_103 (A13[2], B[2], A[13]);
  and and_104 (A13[1], B[1], A[13]);
  and and_105 (A14[1], B[1], A[14]);
  and and_106 (A14[0], B[0], A[14]);
  and and_107 (A15[0], B[0], A[15]);
  and and_108 (A8[4], B[4], A[8]);
  and and_109 (A8[5], B[5], A[8]);
  and and_110 (A9[3], B[3], A[9]);
  and and_111 (A9[4], B[4], A[9]);
  and and_112 (A10[3], B[3], A[10]);
  and and_113 (A10[2], B[2], A[10]);
  and and_114 (A11[1], B[1], A[11]);
  and and_115 (A11[2], B[2], A[11]);
  and and_116 (A12[0], B[0], A[12]);
  and and_117 (A12[1], B[1], A[12]);
  and and_118 (A13[0], B[0], A[13]);
  and and_119 (A8[3], B[3], A[8]);
  and and_120 (A8[2], B[2], A[8]);
  and and_121 (A9[1], B[1], A[9]);
  and and_122 (A9[2], B[2], A[9]);
  and and_123 (A10[0], B[0], A[10]);
  and and_124 (A10[1], B[1], A[10]);
  and and_125 (A11[0], B[0], A[11]);
  and and_126 (A8[1], B[1], A[8]);
  and and_127 (A8[0], B[0], A[8]);
  and and_128 (A9[0], B[0], A[9]);
  and and_129 (A6[15], B[15], A[6]);
  and and_130 (A7[15], B[15], A[7]);
  and and_131 (A7[14], B[14], A[7]);
  and and_132 (A4[15], B[15], A[4]);
  and and_133 (A5[15], B[15], A[5]);
  and and_134 (A5[14], B[14], A[5]);
  and and_135 (A6[14], B[14], A[6]);
  and and_136 (A6[13], B[13], A[6]);
  and and_137 (A7[13], B[13], A[7]);
  and and_138 (A7[12], B[12], A[7]);
  and and_139 (A2[15], B[15], A[2]);
  and and_140 (A3[15], B[15], A[3]);
  and and_141 (A3[14], B[14], A[3]);
  and and_142 (A4[13], B[13], A[4]);
  and and_143 (A4[14], B[14], A[4]);
  and and_144 (A5[13], B[13], A[5]);
  and and_145 (A5[12], B[12], A[5]);
  and and_146 (A6[12], B[12], A[6]);
  and and_147 (A6[11], B[11], A[6]);
  and and_148 (A7[10], B[10], A[7]);
  and and_149 (A7[11], B[11], A[7]);
  and and_150 (A0[14], B[15], A[0]);
  and and_151 (A1[15], B[15], A[1]);
  and and_152 (A1[14], B[14], A[1]);
  and and_153 (A2[14], B[14], A[2]);
  and and_154 (A2[13], B[13], A[2]);
  and and_155 (A3[12], B[12], A[3]);
  and and_156 (A3[13], B[13], A[3]);
  and and_157 (A4[11], B[11], A[4]);
  and and_158 (A4[12], B[12], A[4]);
  and and_159 (A5[10], B[10], A[5]);
  and and_160 (A5[11], B[11], A[5]);
  and and_161 (A6[9], B[9], A[6]);
  and and_162 (A6[10], B[10], A[6]);
  and and_163 (A7[8], B[8], A[7]);
  and and_164 (A7[9], B[9], A[7]);
  and and_165 (A0[13], B[14], A[0]);
  and and_166 (A0[12], B[13], A[0]);
  and and_167 (A1[12], B[12], A[1]);
  and and_168 (A1[13], B[13], A[1]);
  and and_169 (A2[12], B[12], A[2]);
  and and_170 (A2[11], B[11], A[2]);
  and and_171 (A3[10], B[10], A[3]);
  and and_172 (A3[11], B[11], A[3]);
  and and_173 (A4[9], B[9], A[4]);
  and and_174 (A4[10], B[10], A[4]);
  and and_175 (A5[9], B[9], A[5]);
  and and_176 (A5[8], B[8], A[5]);
  and and_177 (A6[7], B[7], A[6]);
  and and_178 (A6[8], B[8], A[6]);
  and and_179 (A7[7], B[7], A[7]);
  and and_180 (A7[6], B[6], A[7]);
  and and_181 (A0[11], B[12], A[0]);
  and and_182 (A0[10], B[11], A[0]);
  and and_183 (A1[11], B[11], A[1]);
  and and_184 (A1[10], B[10], A[1]);
  and and_185 (A2[10], B[10], A[2]);
  and and_186 (A2[9], B[9], A[2]);
  and and_187 (A3[8], B[8], A[3]);
  and and_188 (A3[9], B[9], A[3]);
  and and_189 (A4[7], B[7], A[4]);
  and and_190 (A4[8], B[8], A[4]);
  and and_191 (A5[6], B[6], A[5]);
  and and_192 (A5[7], B[7], A[5]);
  and and_193 (A6[5], B[5], A[6]);
  and and_194 (A6[6], B[6], A[6]);
  and and_195 (A7[4], B[4], A[7]);
  and and_196 (A7[5], B[5], A[7]);
  and and_197 (A0[8], B[9], A[0]);
  and and_198 (A0[9], B[10], A[0]);
  and and_199 (A1[8], B[8], A[1]);
  and and_200 (A1[9], B[9], A[1]);
  and and_201 (A2[7], B[7], A[2]);
  and and_202 (A2[8], B[8], A[2]);
  and and_203 (A3[7], B[7], A[3]);
  and and_204 (A3[6], B[6], A[3]);
  and and_205 (A4[6], B[6], A[4]);
  and and_206 (A4[5], B[5], A[4]);
  and and_207 (A5[5], B[5], A[5]);
  and and_208 (A5[4], B[4], A[5]);
  and and_209 (A6[3], B[3], A[6]);
  and and_210 (A6[4], B[4], A[6]);
  and and_211 (A7[3], B[3], A[7]);
  and and_212 (A7[2], B[2], A[7]);
  and and_213 (A0[6], B[7], A[0]);
  and and_214 (A0[7], B[8], A[0]);
  and and_215 (A1[7], B[7], A[1]);
  and and_216 (A1[6], B[6], A[1]);
  and and_217 (A2[6], B[6], A[2]);
  and and_218 (A2[5], B[5], A[2]);
  and and_219 (A3[5], B[5], A[3]);
  and and_220 (A3[4], B[4], A[3]);
  and and_221 (A4[4], B[4], A[4]);
  and and_222 (A4[3], B[3], A[4]);
  and and_223 (A5[2], B[2], A[5]);
  and and_224 (A5[3], B[3], A[5]);
  and and_225 (A6[2], B[2], A[6]);
  and and_226 (A6[1], B[1], A[6]);
  and and_227 (A7[1], B[1], A[7]);
  and and_228 (A7[0], B[0], A[7]);
  and and_229 (A0[4], B[5], A[0]);
  and and_230 (A0[5], B[6], A[0]);
  and and_231 (A1[4], B[4], A[1]);
  and and_232 (A1[5], B[5], A[1]);
  and and_233 (A2[4], B[4], A[2]);
  and and_234 (A2[3], B[3], A[2]);
  and and_235 (A3[3], B[3], A[3]);
  and and_236 (A3[2], B[2], A[3]);
  and and_237 (A4[2], B[2], A[4]);
  and and_238 (A4[1], B[1], A[4]);
  and and_239 (A5[1], B[1], A[5]);
  and and_240 (A5[0], B[0], A[5]);
  and and_241 (A6[0], B[0], A[6]);
  and and_242 (A0[2], B[3], A[0]);
  and and_243 (A0[3], B[4], A[0]);
  and and_244 (A1[3], B[3], A[1]);
  and and_245 (A1[2], B[2], A[1]);
  and and_246 (A2[1], B[1], A[2]);
  and and_247 (A2[2], B[2], A[2]);
  and and_248 (A3[1], B[1], A[3]);
  and and_249 (A3[0], B[0], A[3]);
  and and_250 (A4[0], B[0], A[4]);
  and and_251 (A0[1], B[2], A[0]);
  and and_252 (A0[0], B[1], A[0]);
  and and_253 (A1[1], B[1], A[1]);
  and and_254 (A1[0], B[0], A[1]);
  and and_255 (A2[0], B[0], A[2]);
  and and_256 (P[0], B[0], A[0]);
  Adder #(.width(16)) adder_1 (
    .a({1'b0, A0}), .b(A1), .out({adder_1_out[14:0], P[1]}), .cin(1'b0), .cout(adder_1_out[15]));
  Adder #(.width(16)) adder_2 (
    .a(adder_1_out), .b(A2), .out({adder_2_out[14:0], P[2]}), .cin(1'b0), .cout(adder_2_out[15]));
  Adder #(.width(16)) adder_3 (
    .a(adder_2_out), .b(A3), .out({adder_3_cout[14:0], P[3]}), .cin(1'b0), .cout(adder_3_cout[15]));
  Adder #(.width(16)) adder_4 (
    .a(adder_3_cout), .b(A4), .out({adder_4_out[14:0], P[4]}), .cin(1'b0), .cout(adder_4_out[15]));
  Adder #(.width(16)) adder_5 (
    .a(adder_4_out), .b(A5), .out({adder_5_out[14:0], P[5]}), .cin(1'b0), .cout(adder_5_out[15]));
  Adder #(.width(16)) adder_6 (
    .a(adder_5_out), .b(A6), .out({adder_6_out[14:0], P[6]}), .cin(1'b0), .cout(adder_6_out[15]));
  Adder #(.width(16)) adder_7 (
    .a(adder_6_out), .b(A7), .out({adder_7_out[14:0], P[7]}), .cin(1'b0), .cout(adder_7_out[15]));
  Adder #(.width(16)) adder_8 (
    .a(adder_7_out), .b(A8), .out({adder_8_out[14:0], P[8]}), .cin(1'b0), .cout(adder_8_out[15]));
  Adder #(.width(16)) adder_9 (
    .a(adder_8_out), .b(A9), .out({adder_9_out[14:0], P[9]}), .cin(1'b0), .cout(adder_9_out[15]));
  Adder #(.width(16)) adder_10 (
    .a(adder_9_out), .b(A10), .out({adder_10_out[14:0], P[10]}), .cin(1'b0), .cout(adder_10_out[15]));
  Adder #(.width(16)) adder_11 (
    .a(adder_10_out), .b(A11), .out({adder_11_cout[14:0], P[11]}), .cin(1'b0), .cout(adder_11_cout[15]));
  Adder #(.width(16)) adder_12 (
    .a(adder_11_cout), .b(A12), .out({adder_12_out[14:0], P[12]}), .cin(1'b0), .cout(adder_12_out[15]));
  Adder #(.width(16)) adder_13 (
    .a(adder_12_out), .b(A13), .out({adder_13_out[14:0], P[13]}), .cin(1'b0), .cout(adder_13_out[15]));
  Adder #(.width(16)) adder_14 (
    .a(adder_13_out), .b(A14), .out({adder_14_out[14:0], P[14]}), .cin(1'b0), .cout(adder_14_out[15]));
  Adder #(.width(16)) adder_15 (.a(adder_14_out), .b(A15), .out(P[30:15]), .cin(1'b0), .cout(P[31]));

  // Notes on the sheet:
  //   16-bit X 16-bit Multiplication Unit
  //   Md. Rifat Ahmed
  //   ID: 1931725042
endmodule

// ALUOp
module ALU_Control (
  input  Binvert,
  input  Ainvert,
  input  F1,
  input  F0,
  output [2:0] ALUOp
);

  wire and_1_out, and_2_out, and_3_out, and_4_out, and_5_out, and_6_out, and_7_out, and_8_out, and_9_out,
       and_10_out, and_11_out, and_12_out, and_13_out, and_14_out, not_1_out, not_2_out, not_3_out, not_4_out;

  not not_1 (not_1_out, Binvert);
  not not_2 (not_2_out, Ainvert);
  not not_3 (not_3_out, F1);
  not not_4 (not_4_out, F0);
  and and_1 (and_1_out, Binvert, F0);
  and and_2 (and_2_out, Binvert, not_3_out);
  and and_3 (and_3_out, not_1_out, F1);
  and and_4 (and_4_out, not_1_out, Ainvert);
  and and_5 (and_5_out, Binvert, not_3_out);
  and and_6 (and_6_out, not_1_out, F1);
  and and_7 (and_7_out, not_1_out, F0);
  and and_8 (and_8_out, not_1_out, Ainvert);
  and and_9 (and_9_out, Binvert, not_2_out, not_4_out);
  and and_10 (and_10_out, not_3_out, not_4_out);
  and and_11 (and_11_out, Binvert, not_3_out);
  and and_12 (and_12_out, not_1_out, Ainvert);
  and and_13 (and_13_out, Binvert, not_2_out);
  and and_14 (and_14_out, not_1_out, F1, F0);
  or O0 (ALUOp[0], and_1_out, and_2_out, and_3_out, and_4_out);
  or O1 (ALUOp[1], and_5_out, and_6_out, and_7_out, and_8_out, and_9_out);
  or O2 (ALUOp[2], and_10_out, and_11_out, and_12_out, and_13_out, and_14_out);

  // Notes on the sheet:
  //   O2 O1 O0
endmodule

// 1-bit ALU
module _1_bit_ALU__7F (
  input  [2:0] ALUOp,
  input  Cin,
  input  A,
  input  Ainvert,
  input  B,
  input  Binvert,
  output Result,
  output Cout
);

  wire adder_1_out, and_1_out, multiplexer_1_out, multiplexer_2_out, not_1_out, not_2_out, or_1_out,
       xor_1_out;

  not not_1 (not_1_out, A);
  not not_2 (not_2_out, B);
  Multiplexer #(.enable("false")) multiplexer_1 (.in0(A), .in1(not_1_out), .out(multiplexer_1_out), .sel(Ainvert));
  Multiplexer #(.enable("false")) multiplexer_2 (.in0(B), .in1(not_2_out), .out(multiplexer_2_out), .sel(Binvert));
  or or_1 (or_1_out, multiplexer_1_out, multiplexer_2_out);
  and and_1 (and_1_out, multiplexer_1_out, multiplexer_2_out);
  xor xor_1 (xor_1_out, multiplexer_1_out, multiplexer_2_out);
  Adder #(.width(1)) adder_1 (.a(multiplexer_1_out), .b(multiplexer_2_out), .out(adder_1_out), .cin(Cin), .cout(Cout));
  Multiplexer #(.select(3), .enable("false")) multiplexer_3 (
    .in0(and_1_out), .in1(or_1_out), .in2(adder_1_out), .in3(adder_1_out), .in4(xor_1_out),
    .in5(adder_1_out), .in6(adder_1_out), .out(Result), .sel(ALUOp));  // open: in7
endmodule

module _32_bit_ALU__7F (
  input  [31:0] A,
  input  [31:0] B,
  input  Ainvert,
  input  Binvert,
  input  [2:0] ALUOp,
  input  Cin,
  output [31:0] Result,
  output Cout,
  output Overflow
);

  wire n1_bit_alu_7f_1_cout, n1_bit_alu_7f_2_cout, n1_bit_alu_7f_3_cout, n1_bit_alu_7f_4_cout,
       n1_bit_alu_7f_5_cout, n1_bit_alu_7f_6_cout, n1_bit_alu_7f_7_cout, n1_bit_alu_7f_8_cout,
       n1_bit_alu_7f_9_cout, n1_bit_alu_7f_10_cout, n1_bit_alu_7f_11_cout, n1_bit_alu_7f_12_cout,
       n1_bit_alu_7f_13_cout, n1_bit_alu_7f_14_cout, n1_bit_alu_7f_15_cout, n1_bit_alu_7f_16_cout,
       n1_bit_alu_7f_17_cout, n1_bit_alu_7f_18_cout, n1_bit_alu_7f_19_cout, n1_bit_alu_7f_20_cout,
       n1_bit_alu_7f_21_cout, n1_bit_alu_7f_22_cout, n1_bit_alu_7f_23_cout, n1_bit_alu_7f_24_cout,
       n1_bit_alu_7f_25_cout, n1_bit_alu_7f_26_cout, n1_bit_alu_7f_27_cout, n1_bit_alu_7f_28_cout,
       n1_bit_alu_7f_29_cout, n1_bit_alu_7f_30_cout, n1_bit_alu_7f_31_cout;

  _1_bit_ALU__7F u_1_bit_alu_7f_1 (
    .ALUOp(ALUOp), .Cin(Cin), .A(A[0]), .Ainvert(Ainvert), .Result(Result[0]), .B(B[0]),
    .Cout(n1_bit_alu_7f_1_cout), .Binvert(Binvert));
  _1_bit_ALU__7F u_1_bit_alu_7f_2 (
    .ALUOp(ALUOp), .Cin(n1_bit_alu_7f_1_cout), .A(A[1]), .Ainvert(Ainvert), .Result(Result[1]), .B(B[1]),
    .Cout(n1_bit_alu_7f_2_cout), .Binvert(Binvert));
  _1_bit_ALU__7F u_1_bit_alu_7f_3 (
    .ALUOp(ALUOp), .Cin(n1_bit_alu_7f_2_cout), .A(A[2]), .Ainvert(Ainvert), .Result(Result[2]), .B(B[2]),
    .Cout(n1_bit_alu_7f_3_cout), .Binvert(Binvert));
  _1_bit_ALU__7F u_1_bit_alu_7f_4 (
    .ALUOp(ALUOp), .Cin(n1_bit_alu_7f_3_cout), .A(A[3]), .Ainvert(Ainvert), .Result(Result[3]), .B(B[3]),
    .Cout(n1_bit_alu_7f_4_cout), .Binvert(Binvert));
  _1_bit_ALU__7F u_1_bit_alu_7f_5 (
    .ALUOp(ALUOp), .Cin(n1_bit_alu_7f_4_cout), .A(A[4]), .Ainvert(Ainvert), .Result(Result[4]), .B(B[4]),
    .Cout(n1_bit_alu_7f_5_cout), .Binvert(Binvert));
  _1_bit_ALU__7F u_1_bit_alu_7f_6 (
    .ALUOp(ALUOp), .Cin(n1_bit_alu_7f_5_cout), .A(A[5]), .Ainvert(Ainvert), .Result(Result[5]), .B(B[5]),
    .Cout(n1_bit_alu_7f_6_cout), .Binvert(Binvert));
  _1_bit_ALU__7F u_1_bit_alu_7f_7 (
    .ALUOp(ALUOp), .Cin(n1_bit_alu_7f_6_cout), .A(A[6]), .Ainvert(Ainvert), .Result(Result[6]), .B(B[6]),
    .Cout(n1_bit_alu_7f_7_cout), .Binvert(Binvert));
  _1_bit_ALU__7F u_1_bit_alu_7f_8 (
    .ALUOp(ALUOp), .Cin(n1_bit_alu_7f_7_cout), .A(A[7]), .Ainvert(Ainvert), .Result(Result[7]), .B(B[7]),
    .Cout(n1_bit_alu_7f_8_cout), .Binvert(Binvert));
  _1_bit_ALU__7F u_1_bit_alu_7f_9 (
    .ALUOp(ALUOp), .Cin(n1_bit_alu_7f_8_cout), .A(A[8]), .Ainvert(Ainvert), .Result(Result[8]), .B(B[8]),
    .Cout(n1_bit_alu_7f_9_cout), .Binvert(Binvert));
  _1_bit_ALU__7F u_1_bit_alu_7f_10 (
    .ALUOp(ALUOp), .Cin(n1_bit_alu_7f_9_cout), .A(A[9]), .Ainvert(Ainvert), .Result(Result[9]), .B(B[9]),
    .Cout(n1_bit_alu_7f_10_cout), .Binvert(Binvert));
  _1_bit_ALU__7F u_1_bit_alu_7f_11 (
    .ALUOp(ALUOp), .Cin(n1_bit_alu_7f_10_cout), .A(A[10]), .Ainvert(Ainvert), .Result(Result[10]), .B(B[10]),
    .Cout(n1_bit_alu_7f_11_cout), .Binvert(Binvert));
  _1_bit_ALU__7F u_1_bit_alu_7f_12 (
    .ALUOp(ALUOp), .Cin(n1_bit_alu_7f_11_cout), .A(A[11]), .Ainvert(Ainvert), .Result(Result[11]), .B(B[11]),
    .Cout(n1_bit_alu_7f_12_cout), .Binvert(Binvert));
  _1_bit_ALU__7F u_1_bit_alu_7f_13 (
    .ALUOp(ALUOp), .Cin(n1_bit_alu_7f_12_cout), .A(A[12]), .Ainvert(Ainvert), .Result(Result[12]), .B(B[12]),
    .Cout(n1_bit_alu_7f_13_cout), .Binvert(Binvert));
  _1_bit_ALU__7F u_1_bit_alu_7f_14 (
    .ALUOp(ALUOp), .Cin(n1_bit_alu_7f_13_cout), .A(A[13]), .Ainvert(Ainvert), .Result(Result[13]), .B(B[13]),
    .Cout(n1_bit_alu_7f_14_cout), .Binvert(Binvert));
  _1_bit_ALU__7F u_1_bit_alu_7f_15 (
    .ALUOp(ALUOp), .Cin(n1_bit_alu_7f_14_cout), .A(A[14]), .Ainvert(Ainvert), .Result(Result[14]), .B(B[14]),
    .Cout(n1_bit_alu_7f_15_cout), .Binvert(Binvert));
  _1_bit_ALU__7F u_1_bit_alu_7f_16 (
    .ALUOp(ALUOp), .Cin(n1_bit_alu_7f_15_cout), .A(A[15]), .Ainvert(Ainvert), .Result(Result[15]), .B(B[15]),
    .Cout(n1_bit_alu_7f_16_cout), .Binvert(Binvert));
  _1_bit_ALU__7F u_1_bit_alu_7f_17 (
    .ALUOp(ALUOp), .Cin(n1_bit_alu_7f_16_cout), .A(A[16]), .Ainvert(Ainvert), .Result(Result[16]), .B(B[16]),
    .Cout(n1_bit_alu_7f_17_cout), .Binvert(Binvert));
  _1_bit_ALU__7F u_1_bit_alu_7f_18 (
    .ALUOp(ALUOp), .Cin(n1_bit_alu_7f_17_cout), .A(A[17]), .Ainvert(Ainvert), .Result(Result[17]), .B(B[17]),
    .Cout(n1_bit_alu_7f_18_cout), .Binvert(Binvert));
  _1_bit_ALU__7F u_1_bit_alu_7f_19 (
    .ALUOp(ALUOp), .Cin(n1_bit_alu_7f_18_cout), .A(A[18]), .Ainvert(Ainvert), .Result(Result[18]), .B(B[18]),
    .Cout(n1_bit_alu_7f_19_cout), .Binvert(Binvert));
  _1_bit_ALU__7F u_1_bit_alu_7f_20 (
    .ALUOp(ALUOp), .Cin(n1_bit_alu_7f_19_cout), .A(A[19]), .Ainvert(Ainvert), .Result(Result[19]), .B(B[19]),
    .Cout(n1_bit_alu_7f_20_cout), .Binvert(Binvert));
  _1_bit_ALU__7F u_1_bit_alu_7f_21 (
    .ALUOp(ALUOp), .Cin(n1_bit_alu_7f_20_cout), .A(A[20]), .Ainvert(Ainvert), .Result(Result[20]), .B(B[20]),
    .Cout(n1_bit_alu_7f_21_cout), .Binvert(Binvert));
  _1_bit_ALU__7F u_1_bit_alu_7f_22 (
    .ALUOp(ALUOp), .Cin(n1_bit_alu_7f_21_cout), .A(A[21]), .Ainvert(Ainvert), .Result(Result[21]), .B(B[21]),
    .Cout(n1_bit_alu_7f_22_cout), .Binvert(Binvert));
  _1_bit_ALU__7F u_1_bit_alu_7f_23 (
    .ALUOp(ALUOp), .Cin(n1_bit_alu_7f_22_cout), .A(A[22]), .Ainvert(Ainvert), .Result(Result[22]), .B(B[22]),
    .Cout(n1_bit_alu_7f_23_cout), .Binvert(Binvert));
  _1_bit_ALU__7F u_1_bit_alu_7f_24 (
    .ALUOp(ALUOp), .Cin(n1_bit_alu_7f_23_cout), .A(A[23]), .Ainvert(Ainvert), .Result(Result[23]), .B(B[23]),
    .Cout(n1_bit_alu_7f_24_cout), .Binvert(Binvert));
  _1_bit_ALU__7F u_1_bit_alu_7f_25 (
    .ALUOp(ALUOp), .Cin(n1_bit_alu_7f_24_cout), .A(A[24]), .Ainvert(Ainvert), .Result(Result[24]), .B(B[24]),
    .Cout(n1_bit_alu_7f_25_cout), .Binvert(Binvert));
  _1_bit_ALU__7F u_1_bit_alu_7f_26 (
    .ALUOp(ALUOp), .Cin(n1_bit_alu_7f_25_cout), .A(A[25]), .Ainvert(Ainvert), .Result(Result[25]), .B(B[25]),
    .Cout(n1_bit_alu_7f_26_cout), .Binvert(Binvert));
  _1_bit_ALU__7F u_1_bit_alu_7f_27 (
    .ALUOp(ALUOp), .Cin(n1_bit_alu_7f_26_cout), .A(A[26]), .Ainvert(Ainvert), .Result(Result[26]), .B(B[26]),
    .Cout(n1_bit_alu_7f_27_cout), .Binvert(Binvert));
  _1_bit_ALU__7F u_1_bit_alu_7f_28 (
    .ALUOp(ALUOp), .Cin(n1_bit_alu_7f_27_cout), .A(A[27]), .Ainvert(Ainvert), .Result(Result[27]), .B(B[27]),
    .Cout(n1_bit_alu_7f_28_cout), .Binvert(Binvert));
  _1_bit_ALU__7F u_1_bit_alu_7f_29 (
    .ALUOp(ALUOp), .Cin(n1_bit_alu_7f_28_cout), .A(A[28]), .Ainvert(Ainvert), .Result(Result[28]), .B(B[28]),
    .Cout(n1_bit_alu_7f_29_cout), .Binvert(Binvert));
  _1_bit_ALU__7F u_1_bit_alu_7f_30 (
    .ALUOp(ALUOp), .Cin(n1_bit_alu_7f_29_cout), .A(A[29]), .Ainvert(Ainvert), .Result(Result[29]), .B(B[29]),
    .Cout(n1_bit_alu_7f_30_cout), .Binvert(Binvert));
  _1_bit_ALU__7F u_1_bit_alu_7f_31 (
    .ALUOp(ALUOp), .Cin(n1_bit_alu_7f_30_cout), .A(A[30]), .Ainvert(Ainvert), .Result(Result[30]), .B(B[30]),
    .Cout(n1_bit_alu_7f_31_cout), .Binvert(Binvert));
  _1_bit_ALU__7F u_1_bit_alu_7f_32 (
    .ALUOp(ALUOp), .Cin(n1_bit_alu_7f_31_cout), .A(A[31]), .Ainvert(Ainvert), .Result(Result[31]), .B(B[31]),
    .Cout(Cout), .Binvert(Binvert));
  xor xor_1 (Overflow, n1_bit_alu_7f_31_cout, Cout);

  // Other names for the same wires on the sheet: S0 = Result[0]; S1 = Result[1]; S2 = Result[2]; S3 = Result[3];
  //   S4 = Result[4]; S5 = Result[5]; S6 = Result[6]; S7 = Result[7]; S8 = Result[8]; S9 = Result[9];
  //   S10 = Result[10]; S11 = Result[11]; S12 = Result[12]; S13 = Result[13]; S14 = Result[14]; S15 = Result[15];
  //   S16 = Result[16]; S17 = Result[17]; S18 = Result[18]; S19 = Result[19]; S20 = Result[20]; S21 = Result[21];
  //   S22 = Result[22]; S23 = Result[23]; S24 = Result[24]; S25 = Result[25]; S26 = Result[26]; S27 = Result[27];
  //   S28 = Result[28]; S29 = Result[29]; S30 = Result[30]; S31 = Result[31]
endmodule

module _32_bit_ALU (
  input  Cin,
  input  [5:0] F,
  input  [31:0] A,
  input  Ainvert,
  input  [31:0] B,
  input  Binvert,
  output [31:0] Result,
  output Cout,
  output Overflow,
  output Zero
);

  wire or_1_out;
  wire [2:0] alu_control_1_aluop;
  wire [31:0] n32_bit_alu_7f_1_result, n32_bit_multiplier_1_p;

  ALU_Control alu_control_1 (.Binvert(Binvert), .Ainvert(Ainvert), .F1(F[1]), .F0(F[0]), .ALUOp(alu_control_1_aluop));
  _32_bit_Multiplier u_32_bit_multiplier_1 (.A(A[15:0]), .B(B[15:0]), .P(n32_bit_multiplier_1_p));
  _32_bit_ALU__7F u_32_bit_alu_7f_1 (
    .A(A), .B(B), .Ainvert(Ainvert), .Binvert(Binvert), .ALUOp(alu_control_1_aluop), .Cin(Cin),
    .Result(n32_bit_alu_7f_1_result), .Cout(Cout), .Overflow(Overflow));
  DotMatrix #(.matrixcols(3), .matrixrows(1)) dotmatrix_1 (
    .col0(alu_control_1_aluop[2]), .col1(alu_control_1_aluop[1]), .col2(alu_control_1_aluop[0]));
  Multiplexer #(.select(3), .width(32), .enable("false")) multiplexer_1 (
    .in0(n32_bit_alu_7f_1_result), .in1(n32_bit_alu_7f_1_result), .in2(n32_bit_alu_7f_1_result),
    .in3(n32_bit_alu_7f_1_result), .in4(n32_bit_alu_7f_1_result), .in5(n32_bit_alu_7f_1_result),
    .in6(n32_bit_alu_7f_1_result), .in7(n32_bit_multiplier_1_p), .out(Result), .sel(alu_control_1_aluop));
  or or_1 (or_1_out, Result[0], Result[1], Result[2], Result[3], Result[4], Result[5], Result[6], Result[7], Result[8], Result[9], Result[10], Result[11], Result[12], Result[13], Result[14], Result[15], Result[17], Result[18], Result[19], Result[20], Result[21], Result[22], Result[23], Result[24], Result[25], Result[26], Result[27], Result[28], Result[29], Result[30], Result[31], Result[16]);
  not not_1 (Zero, or_1_out);
endmodule
