// Logisim project Lab 9.circ as structural Verilog: 1 circuit, main circuit main
module main (
  input  in_1,
  input  DOWN,
  output A0,
  output out_4,
  output A2,
  output A3
);

  wire and_1_out, and_2_out, and_3_out, and_4_out, and_5_out, and_6_out, and_7_out, button_1_out,
       clock_1_out, d_ff_1_qn, d_ff_2_qn, d_ff_3_qn, not_1_out, or_1_out, or_2_out, or_3_out, or_4_out,
       or_5_out, xor_1_out, xor_2_out, xor_3_out;

  not not_1 (not_1_out, in_1);
  and and_1 (and_1_out, not_1_out, DOWN);
  and and_2 (and_2_out, and_1_out, d_ff_1_qn);
  and and_3 (and_3_out, and_2_out, d_ff_2_qn);
  and and_4 (and_4_out, and_3_out, d_ff_3_qn);
  or or_1 (or_1_out, in_1, and_1_out);
  and and_5 (and_5_out, in_1, A0);
  and and_6 (and_6_out, and_5_out, out_4);
  and and_7 (and_7_out, and_6_out, A2);
  or or_2 (or_2_out, and_5_out, and_2_out);
  or or_3 (or_3_out, and_6_out, and_3_out);
  or or_4 (or_4_out, and_7_out, and_4_out);
  xor xor_1 (xor_1_out, A0, or_1_out);
  xor xor_2 (xor_2_out, out_4, or_2_out);
  xor xor_3 (xor_3_out, A2, or_3_out);
  or or_5 (or_5_out, A3, or_4_out);
  Clock clock_1 (.out(clock_1_out));
  D_Flip_Flop d_ff_1 (
    .clk(clock_1_out), .D(xor_1_out), .Q(A0), .Qn(d_ff_1_qn), .reset(button_1_out));  // open: preset, en
  D_Flip_Flop d_ff_2 (
    .clk(clock_1_out), .D(xor_2_out), .Q(out_4), .Qn(d_ff_2_qn), .reset(button_1_out));  // open: preset, en
  D_Flip_Flop d_ff_3 (
    .clk(clock_1_out), .D(xor_3_out), .Q(A2), .Qn(d_ff_3_qn), .reset(button_1_out));  // open: preset, en
  D_Flip_Flop d_ff_4 (.clk(clock_1_out), .D(or_5_out), .Q(A3), .reset(button_1_out));  // open: Qn, preset, en
  Button button_1 (.out(button_1_out));

  // Notes on the sheet:
  //   UP
  //                CLOCK
  //            RESET
  //    A1
endmodule
